// Logisim project Logisim cpu.circ as structural Verilog: 16 circuits, main circuit main
module main (
  input  in_1,
  output [31:0] out_2,
  output out_3,
  output [4:0] out_4,
  output [31:0] out_5,
  output out_6,
  output [4:0] out_7,
  output [31:0] out_8
);

  wire ALU_SRC, and_1_out, clk, equal, J, MemToReg, NPc_sel, reg_Dst;
  wire [2:0] ALU_Op, EXT_Op;
  wire [4:0] rs, rt;
  wire [5:0] splitter_1_out_7;
  wire [15:0] imm16;
  wire [31:0] alu_1_out_5, ext_1_imm32, grf_1_out_8, multiplexer_2_out, ram_1_data;

  Clock clock_1 (.out(clk));
  Multiplexer #(.width(5), .disabled(0), .enable("false")) multiplexer_1 (
    .in0(rt), .in1(imm16[15:11]), .out(out_4), .sel(reg_Dst));
  and and_1 (and_1_out, NPc_sel, equal);
  IFU ifu_1 (.J(J), .\tran (and_1_out), .clk(clk), .reset(in_1), .opcode(out_2));
  grf grf_1 (
    .WE(out_3), .a1(rs), .a2(rt), .a3(out_4), .WD(out_5), .out_8(grf_1_out_8), .out_9(out_8), .in_2(clk),
    .reset(in_1));
  splitter splitter_1 (
    .in_1(out_2), .out_2(imm16[5:0]), .out_3(imm16[10:6]), .out_4(imm16[15:11]), .out_5(rt), .out_6(rs),
    .out_7(splitter_1_out_7));
  Multiplexer #(.width(32), .disabled(0), .enable("false")) multiplexer_2 (
    .in0(out_8), .in1(ext_1_imm32), .out(multiplexer_2_out), .sel(ALU_SRC));
  EXT ext_1 (.imm16(imm16), .in_2(EXT_Op), .imm32(ext_1_imm32));
  Multiplexer #(.width(32), .disabled(0), .enable("false")) multiplexer_3 (
    .in0({alu_1_out_5[31:7], out_7, alu_1_out_5[1:0]}), .in1(ram_1_data), .out(out_5), .sel(MemToReg));
  Controller1 controller1_1 (
    .Op(splitter_1_out_7), .Reg_DST(reg_Dst), .Func(imm16[5:0]), .Reg_Write(out_3), .ALU_SRC(ALU_SRC),
    .Mem_to_Reg(MemToReg), .Mem_Write(out_6), .NPC_Sel(NPc_sel), .EXT_Op(EXT_Op), .ALU_Op(ALU_Op), .j(J));
  ALU alu_1 (
    .in_1(grf_1_out_8), .in_2(multiplexer_2_out), .in_3(ALU_Op),
    .out_5({alu_1_out_5[31:7], out_7, alu_1_out_5[1:0]}));  // open: out_4
  // Probe on ALU_Op
  Comparator #(.width(32)) comparator_1 (
    .a({alu_1_out_5[31:7], out_7, alu_1_out_5[1:0]}), .b(32'h1), .eq(equal));  // open: gt, lt
  RAM #(.addrWidth(5), .dataWidth(32), .bus("separate")) ram_1 (
    .addr(out_7), .din(out_8), .data(ram_1_data), .str(out_6), .clk(clk), .ld(MemToReg), .clr(in_1));  // open: sel

  // Other names for the same wires on the sheet: MemAddr[4:0] = out_7; rd[4:0] = imm16[15:11]; Instr[31:0] = out_2;
  //   Mem_Write = out_6; MemData[31:0] = out_8; reg_Write = out_3; RegAddr[4:0] = out_4; RegData[31:0] = out_5;
  //   Reset = in_1
endmodule

module IFU (
  input  J,
  input  \tran ,
  input  clk,
  input  reset,
  output [31:0] opcode
);

  wire [31:0] adder_1_out, adder_2_out, bit_extender_1_out, multiplexer_1_out, multiplexer_2_out,
       register_1_q;

  Register #(.width(32)) register_1 (.D(multiplexer_2_out), .Q(register_1_q), .clk(clk), .clr(reset));  // open: en
  Adder #(.width(32)) adder_1 (.a(register_1_q), .b(32'h4), .out(adder_1_out));  // open: cin, cout
  ROM #(.addrWidth(5), .dataWidth(32)) rom_1 (.addr(register_1_q[6:2]), .data(opcode));  // open: sel
  assign bit_extender_1_out = {{14{1'b0}}, {opcode[15:0], 2'b00}};  // Bit_Extender bit_extender_1
  Adder #(.width(32)) adder_2 (.a(bit_extender_1_out), .b(adder_1_out), .out(adder_2_out));  // open: cin, cout
  Multiplexer #(.width(32), .enable("false")) multiplexer_1 (
    .in0(adder_1_out), .in1(adder_2_out), .out(multiplexer_1_out), .sel(\tran ));
  Multiplexer #(.width(32), .enable("false")) multiplexer_2 (
    .in0(multiplexer_1_out), .in1({opcode[31:28], opcode[25:0], 2'b00}), .out(multiplexer_2_out), .sel(J));
  // Probe on multiplexer_2_out

  // Other names for the same wires on the sheet: first[3:0] = opcode[31:28]

  // Notes on the sheet:
  //   contents of rom_1 (hex, n*v repeats v):
  //   3c010000 34210003 1014021 11280005 1495021 3c010000 34210001 1214821 8000c03 3c010000 34210006
  //   1415023
endmodule

module splitter (
  input  [31:0] in_1,
  output [5:0] out_2,
  output [4:0] out_3,
  output [4:0] out_4,
  output [4:0] out_5,
  output [4:0] out_6,
  output [5:0] out_7
);


  assign out_2 = in_1[5:0];
  assign out_3 = in_1[10:6];
  assign out_4 = in_1[15:11];
  assign out_5 = in_1[20:16];
  assign out_6 = in_1[25:21];
  assign out_7 = in_1[31:26];
endmodule

module Controller1 (
  input  [5:0] Op,
  input  [5:0] Func,
  output Reg_DST,
  output Reg_Write,
  output ALU_SRC,
  output Mem_to_Reg,
  output Mem_Write,
  output NPC_Sel,
  output [2:0] EXT_Op,
  output [2:0] ALU_Op,
  output j
);

  wire and_log_1_addu, and_log_1_beq, and_log_1_blez, and_log_1_j, and_log_1_lui, and_log_1_lw,
       and_log_1_ori, and_log_1_subu, and_log_1_sw;

  AND_Log and_log_1 (
    .SubU(and_log_1_subu), .AddU(and_log_1_addu), .Ori(and_log_1_ori), .LW(and_log_1_lw), .SW(and_log_1_sw),
    .Beq(and_log_1_beq), .LUI(and_log_1_lui), .Op_5(Op[5]), .Op_4(Op[4]), .Op_3(Op[3]), .Op_2(Op[2]),
    .Op_1(Op[1]), .Op_0(Op[0]), .Func_5(Func[5]), .Func_4(Func[4]), .Func_3(Func[3]), .Func_2(Func[2]),
    .Func_1(Func[1]), .Func_0(Func[0]), .Blez(and_log_1_blez), .j(and_log_1_j));
  OR_log or_log_1 (
    .AddU(and_log_1_subu), .SubU(and_log_1_addu), .Ori(and_log_1_ori), .LW(and_log_1_lw), .SW(and_log_1_sw),
    .Beq(and_log_1_beq), .Blez(and_log_1_blez), .LUI(and_log_1_lui), .ALU_OP(ALU_Op), .Reg_DST(Reg_DST),
    .Reg_Write(Reg_Write), .ALU_SRC(ALU_SRC), .Mem_to_Reg(Mem_to_Reg), .Mem_Write(Mem_Write),
    .NPC_Sel(NPC_Sel), .EXT_Op(EXT_Op), .J(and_log_1_j), .j_2(j));
endmodule

module AND_Log (
  input  Op_5,
  input  Op_4,
  input  Op_3,
  input  Op_2,
  input  Op_1,
  input  Op_0,
  input  Func_5,
  input  Func_4,
  input  Func_3,
  input  Func_2,
  input  Func_1,
  input  Func_0,
  output SubU,
  output AddU,
  output Ori,
  output LW,
  output SW,
  output Beq,
  output Blez,
  output LUI,
  output j
);

  wire not_1_out, not_2_out, not_3_out, not_4_out, not_5_out, not_6_out, not_7_out, not_8_out, not_9_out,
       not_10_out, not_11_out, not_12_out;

  not not_1 (not_1_out, Op_5);
  not not_2 (not_2_out, Op_3);
  not not_3 (not_3_out, Op_4);
  not not_4 (not_4_out, Op_1);
  not not_5 (not_5_out, Op_2);
  not not_6 (not_6_out, Op_0);
  not not_7 (not_7_out, Func_5);
  not not_8 (not_8_out, Func_3);
  not not_9 (not_9_out, Func_4);
  not not_10 (not_10_out, Func_2);
  not not_11 (not_11_out, Func_1);
  not not_12 (not_12_out, Func_0);
  and u_SubU (SubU, not_1_out, not_3_out, not_2_out, not_5_out, not_4_out, not_6_out, Func_5, not_9_out, not_8_out, not_10_out, Func_1, Func_0);
  and u_AddU (AddU, not_1_out, not_3_out, not_2_out, not_5_out, not_4_out, not_6_out, Func_5, not_9_out, not_8_out, not_10_out, not_11_out, Func_0);
  and u_Ori (Ori, not_1_out, not_3_out, Op_3, Op_2, not_4_out, Op_0);
  and u_LW (LW, Op_5, not_3_out, not_2_out, not_5_out, Op_1, Op_0);
  and u_SW (SW, Op_5, not_3_out, Op_3, not_5_out, Op_1, Op_0);
  and u_Beq (Beq, not_1_out, not_3_out, not_2_out, Op_2, not_4_out, not_6_out);
  and Blex (Blez, not_1_out, not_3_out, not_2_out, Op_2, Op_1, not_6_out);
  and u_LUI (LUI, not_1_out, not_3_out, Op_3, Op_2, Op_1, Op_0);
  and u_j (j, not_1_out, not_2_out, not_5_out, Op_1, not_6_out, not_3_out);
endmodule

module OR_log (
  input  AddU,
  input  SubU,
  input  Ori,
  input  LW,
  input  SW,
  input  Beq,
  input  Blez,
  input  LUI,
  input  J,
  output j_2,
  output Reg_DST,
  output Reg_Write,
  output ALU_SRC,
  output Mem_to_Reg,
  output Mem_Write,
  output NPC_Sel,
  output [2:0] EXT_Op,
  output [2:0] ALU_OP
);

  or or_1 (Reg_DST, AddU, SubU);
  or or_2 (Reg_Write, AddU, SubU, LUI, Ori, LW);
  or or_3 (ALU_SRC, Ori, LW, SW, LUI);
  buf or_4 (Mem_to_Reg, LW);  // OR_Gate
  buf or_5 (Mem_Write, SW);  // OR_Gate
  buf or_6 (NPC_Sel, Beq);  // OR_Gate
  buf or_7 (EXT_Op[1], LUI);  // OR_Gate
  or or_8 (EXT_Op[0], LW, SW);
  or or_9 (ALU_OP[1], Beq, Ori);
  or or_10 (ALU_OP[0], Beq, AddU);

  assign ALU_OP[2] = 1'b0;
  assign EXT_Op[2] = 1'b0;
  assign j_2 = J;
endmodule

module ALU (
  input  [31:0] in_1,
  input  [31:0] in_2,
  input  [2:0] in_3,
  output out_4,
  output [31:0] out_5
);

  wire adder_1_cout, subtractor_1_bout;
  wire [0:0] comparator_1_eq;
  wire [31:0] adder_1_out, or_1_out, subtractor_1_out;

  Comparator #(.width(32), .mode("unsigned")) comparator_1 (
    .a(in_1), .b(in_2), .eq(comparator_1_eq[0]));  // open: gt, lt
  Adder #(.width(32)) adder_1 (.a(in_1), .b(in_2), .out(adder_1_out), .cout(adder_1_cout));  // open: cin
  Subtractor #(.width(32)) subtractor_1 (
    .a(in_1), .b(in_2), .out(subtractor_1_out), .bout(subtractor_1_bout));  // open: bin
  assign or_1_out = in_1 | in_2;  // OR_Gate or_1, 32 bits wide
  Multiplexer #(.select(3), .width(32), .enable("false")) multiplexer_1 (
    .in0(adder_1_out), .in1(subtractor_1_out), .in2(or_1_out), .in3({{31{1'b0}}, comparator_1_eq[0]}),
    .out(out_5), .sel(in_3));  // open: in4, in5, in6, in7
  Multiplexer #(.select(3), .enable("false")) multiplexer_2 (
    .in0(adder_1_cout), .in1(subtractor_1_bout), .out(out_4), .sel(in_3));  // open: in2, in3, in4, in5, in6, in7
endmodule

module _32bit_adder (
  input  [31:0] B,
  input  [31:0] A,
  output jinwei,
  output [31:0] Sum
);

  wire n1bit_addr_2_out_5, n1bit_addr_3_out_5, n1bit_addr_4_out_5, n1bit_addr_5_out_5, n1bit_addr_6_out_5,
       n1bit_addr_7_out_5, n1bit_addr_8_out_5, n1bit_addr_9_out_5, n1bit_addr_10_out_5, n1bit_addr_11_out_5,
       n1bit_addr_12_out_5, n1bit_addr_13_out_5, n1bit_addr_14_out_5, n1bit_addr_15_out_5,
       n1bit_addr_16_out_5, n1bit_addr_17_out_5, n1bit_addr_18_out_5, n1bit_addr_19_out_5,
       n1bit_addr_20_out_5, n1bit_addr_21_out_5, n1bit_addr_22_out_5, n1bit_addr_23_out_5,
       n1bit_addr_24_out_5, n1bit_addr_25_out_5, n1bit_addr_26_out_5, n1bit_addr_27_out_5,
       n1bit_addr_28_out_5, n1bit_addr_29_out_5, n1bit_addr_30_out_5, n1bit_addr_31_out_5,
       n1bit_addr_32_out_5;

  _1bit_addr u_1bit_addr_1 (.a_i(A[31]), .b_i(B[31]), .c_i(n1bit_addr_2_out_5), .out_4(Sum[31]), .out_5(jinwei));
  _1bit_addr u_1bit_addr_2 (
    .a_i(A[30]), .b_i(B[30]), .c_i(n1bit_addr_3_out_5), .out_4(Sum[30]), .out_5(n1bit_addr_2_out_5));
  _1bit_addr u_1bit_addr_3 (
    .a_i(A[29]), .b_i(B[29]), .c_i(n1bit_addr_4_out_5), .out_4(Sum[29]), .out_5(n1bit_addr_3_out_5));
  _1bit_addr u_1bit_addr_4 (
    .a_i(A[28]), .b_i(B[28]), .c_i(n1bit_addr_5_out_5), .out_4(Sum[28]), .out_5(n1bit_addr_4_out_5));
  _1bit_addr u_1bit_addr_5 (
    .a_i(A[27]), .b_i(B[27]), .c_i(n1bit_addr_6_out_5), .out_4(Sum[27]), .out_5(n1bit_addr_5_out_5));
  _1bit_addr u_1bit_addr_6 (
    .a_i(A[26]), .b_i(B[26]), .c_i(n1bit_addr_7_out_5), .out_4(Sum[26]), .out_5(n1bit_addr_6_out_5));
  _1bit_addr u_1bit_addr_7 (
    .a_i(A[25]), .b_i(B[25]), .c_i(n1bit_addr_8_out_5), .out_4(Sum[25]), .out_5(n1bit_addr_7_out_5));
  _1bit_addr u_1bit_addr_8 (
    .a_i(A[24]), .b_i(B[24]), .c_i(n1bit_addr_9_out_5), .out_4(Sum[24]), .out_5(n1bit_addr_8_out_5));
  _1bit_addr u_1bit_addr_9 (
    .a_i(A[23]), .b_i(B[23]), .c_i(n1bit_addr_10_out_5), .out_4(Sum[23]), .out_5(n1bit_addr_9_out_5));
  _1bit_addr u_1bit_addr_10 (
    .a_i(A[22]), .b_i(B[22]), .c_i(n1bit_addr_11_out_5), .out_4(Sum[22]), .out_5(n1bit_addr_10_out_5));
  _1bit_addr u_1bit_addr_11 (
    .a_i(A[21]), .b_i(B[21]), .c_i(n1bit_addr_12_out_5), .out_4(Sum[21]), .out_5(n1bit_addr_11_out_5));
  _1bit_addr u_1bit_addr_12 (
    .a_i(A[20]), .b_i(B[20]), .c_i(n1bit_addr_13_out_5), .out_4(Sum[20]), .out_5(n1bit_addr_12_out_5));
  _1bit_addr u_1bit_addr_13 (
    .a_i(A[19]), .b_i(B[19]), .c_i(n1bit_addr_14_out_5), .out_4(Sum[19]), .out_5(n1bit_addr_13_out_5));
  _1bit_addr u_1bit_addr_14 (
    .a_i(A[18]), .b_i(B[18]), .c_i(n1bit_addr_15_out_5), .out_4(Sum[18]), .out_5(n1bit_addr_14_out_5));
  _1bit_addr u_1bit_addr_15 (
    .a_i(A[17]), .b_i(B[17]), .c_i(n1bit_addr_16_out_5), .out_4(Sum[17]), .out_5(n1bit_addr_15_out_5));
  _1bit_addr u_1bit_addr_16 (
    .a_i(A[16]), .b_i(B[16]), .c_i(n1bit_addr_17_out_5), .out_4(Sum[16]), .out_5(n1bit_addr_16_out_5));
  _1bit_addr u_1bit_addr_17 (
    .a_i(A[15]), .b_i(B[15]), .c_i(n1bit_addr_18_out_5), .out_4(Sum[15]), .out_5(n1bit_addr_17_out_5));
  _1bit_addr u_1bit_addr_18 (
    .a_i(A[14]), .b_i(B[14]), .c_i(n1bit_addr_19_out_5), .out_4(Sum[14]), .out_5(n1bit_addr_18_out_5));
  _1bit_addr u_1bit_addr_19 (
    .a_i(A[13]), .b_i(B[13]), .c_i(n1bit_addr_20_out_5), .out_4(Sum[13]), .out_5(n1bit_addr_19_out_5));
  _1bit_addr u_1bit_addr_20 (
    .a_i(A[12]), .b_i(B[12]), .c_i(n1bit_addr_21_out_5), .out_4(Sum[12]), .out_5(n1bit_addr_20_out_5));
  _1bit_addr u_1bit_addr_21 (
    .a_i(A[11]), .b_i(B[11]), .c_i(n1bit_addr_22_out_5), .out_4(Sum[11]), .out_5(n1bit_addr_21_out_5));
  _1bit_addr u_1bit_addr_22 (
    .a_i(A[10]), .b_i(B[10]), .c_i(n1bit_addr_23_out_5), .out_4(Sum[10]), .out_5(n1bit_addr_22_out_5));
  _1bit_addr u_1bit_addr_23 (
    .a_i(A[9]), .b_i(B[9]), .c_i(n1bit_addr_24_out_5), .out_4(Sum[9]), .out_5(n1bit_addr_23_out_5));
  _1bit_addr u_1bit_addr_24 (
    .a_i(A[8]), .b_i(B[8]), .c_i(n1bit_addr_25_out_5), .out_4(Sum[8]), .out_5(n1bit_addr_24_out_5));
  _1bit_addr u_1bit_addr_25 (
    .a_i(A[7]), .b_i(B[7]), .c_i(n1bit_addr_26_out_5), .out_4(Sum[7]), .out_5(n1bit_addr_25_out_5));
  _1bit_addr u_1bit_addr_26 (
    .a_i(A[6]), .b_i(B[6]), .c_i(n1bit_addr_27_out_5), .out_4(Sum[6]), .out_5(n1bit_addr_26_out_5));
  _1bit_addr u_1bit_addr_27 (
    .a_i(A[5]), .b_i(B[5]), .c_i(n1bit_addr_28_out_5), .out_4(Sum[5]), .out_5(n1bit_addr_27_out_5));
  _1bit_addr u_1bit_addr_28 (
    .a_i(A[4]), .b_i(B[4]), .c_i(n1bit_addr_29_out_5), .out_4(Sum[4]), .out_5(n1bit_addr_28_out_5));
  _1bit_addr u_1bit_addr_29 (
    .a_i(A[3]), .b_i(B[3]), .c_i(n1bit_addr_30_out_5), .out_4(Sum[3]), .out_5(n1bit_addr_29_out_5));
  _1bit_addr u_1bit_addr_30 (
    .a_i(A[2]), .b_i(B[2]), .c_i(n1bit_addr_31_out_5), .out_4(Sum[2]), .out_5(n1bit_addr_30_out_5));
  _1bit_addr u_1bit_addr_31 (
    .a_i(A[1]), .b_i(B[1]), .c_i(n1bit_addr_32_out_5), .out_4(Sum[1]), .out_5(n1bit_addr_31_out_5));
  _1bit_addr u_1bit_addr_32 (.a_i(B[0]), .b_i(A[0]), .c_i(1'b0), .out_4(Sum[0]), .out_5(n1bit_addr_32_out_5));

  // Other names for the same wires on the sheet: s0 = Sum[0]; s1 = Sum[1]; s2 = Sum[2]; s3 = Sum[3]; s4 = Sum[4];
  //   s5 = Sum[5]; s6 = Sum[6]; s7 = Sum[7]; s8 = Sum[8]; s9 = Sum[9]; s10 = Sum[10]; s11 = Sum[11]; s12 = Sum[12];
  //   s13 = Sum[13]; s14 = Sum[14]; s15 = Sum[15]; s16 = Sum[16]; s17 = Sum[17]; s18 = Sum[18]; s19 = Sum[19];
  //   s20 = Sum[20]; s21 = Sum[21]; s22 = Sum[22]; s23 = Sum[23]; s24 = Sum[24]; s25 = Sum[25]; s26 = Sum[26];
  //   s27 = Sum[27]; s28 = Sum[28]; s29 = Sum[29]; s30 = Sum[30]; s31 = Sum[31]
endmodule

module _32bit_sub (
  input  [31:0] A,
  input  [31:0] B,
  output [31:0] out_3
);

  wire [31:0] n32bit_adder_1_sum, not_1_out;

  assign not_1_out = ~B;  // NOT_Gate not_1, 32 bits wide
  _32bit_adder u_32bit_adder_1 (.B(32'h1), .A(not_1_out), .Sum(n32bit_adder_1_sum));  // open: jinwei
  _32bit_adder u_32bit_adder_2 (.B(n32bit_adder_1_sum), .A(A), .Sum(out_3));  // open: jinwei

  // Notes on the sheet:
  //   A
  //   B
endmodule

module _1bit_addr (
  input  a_i,
  input  b_i,
  input  c_i,
  output out_4,
  output out_5
);

  wire and_1_out, and_2_out, and_3_out;

  xor xor_1 (out_4, a_i, b_i, c_i);
  and and_1 (and_1_out, a_i, b_i);
  and and_2 (and_2_out, a_i, c_i);
  and and_3 (and_3_out, b_i, c_i);
  or or_1 (out_5, and_1_out, and_2_out, and_3_out);
endmodule

module EXT (
  input  [15:0] imm16,
  input  [2:0] in_2,
  output [31:0] imm32
);

  wire [31:0] bit_extender_1_out, bit_extender_2_out, bit_extender_3_out;

  assign bit_extender_1_out = {{16{1'b0}}, imm16};  // Bit_Extender bit_extender_1
  assign bit_extender_2_out = {{16{imm16[15]}}, imm16};  // Bit_Extender bit_extender_2
  assign bit_extender_3_out = {{16{1'b0}}, imm16};  // Bit_Extender bit_extender_3
  Multiplexer #(.select(3), .width(32), .enable("false")) multiplexer_1 (
    .in0(bit_extender_1_out), .in1(bit_extender_2_out),
    .in2({bit_extender_3_out[15:0], bit_extender_3_out[31:16]}), .out(imm32), .sel(in_2));  // open: in3, in4, in5, in6, in7
endmodule

module grf (
  input  WE,
  input  in_2,
  input  reset,
  input  [4:0] a1,
  input  [4:0] a2,
  input  [4:0] a3,
  input  [31:0] WD,
  output [31:0] out_8,
  output [31:0] out_9
);

  wire [31:0] decoder_1_out0, n8_register_1_out_13, n8_register_1_out_14, n8_register_1_out_15,
       n8_register_1_out_16, n8_register_1_out_17, n8_register_1_out_18, n8_register_1_out_19,
       n8_register_1_out_20, n8_register_2_out_13, n8_register_2_out_14, n8_register_2_out_15,
       n8_register_2_out_16, n8_register_2_out_17, n8_register_2_out_18, n8_register_2_out_19,
       n8_register_2_out_20, n8_register_3_out_13, n8_register_3_out_14, n8_register_3_out_15,
       n8_register_3_out_16, n8_register_3_out_17, n8_register_3_out_18, n8_register_3_out_19,
       n8_register_3_out_20, s0_s7_1_out_13, s0_s7_1_out_14, s0_s7_1_out_15, s0_s7_1_out_16, s0_s7_1_out_17,
       s0_s7_1_out_18, s0_s7_1_out_19, s0_s7_1_out_20;

  Decoder #(.select(5), .disabled(0)) decoder_1 (
    .out0(decoder_1_out0[0]), .out1(decoder_1_out0[1]), .out2(decoder_1_out0[2]), .out3(decoder_1_out0[3]),
    .out4(decoder_1_out0[4]), .out5(decoder_1_out0[5]), .out6(decoder_1_out0[6]), .out7(decoder_1_out0[7]),
    .out8(decoder_1_out0[8]), .out9(decoder_1_out0[9]), .out10(decoder_1_out0[10]),
    .out11(decoder_1_out0[11]), .out12(decoder_1_out0[12]), .out13(decoder_1_out0[13]),
    .out14(decoder_1_out0[14]), .out15(decoder_1_out0[15]), .out16(decoder_1_out0[16]),
    .out17(decoder_1_out0[17]), .out18(decoder_1_out0[18]), .out19(decoder_1_out0[19]),
    .out20(decoder_1_out0[20]), .out21(decoder_1_out0[21]), .out22(decoder_1_out0[22]),
    .out23(decoder_1_out0[23]), .out24(decoder_1_out0[24]), .out25(decoder_1_out0[25]),
    .out26(decoder_1_out0[26]), .out27(decoder_1_out0[27]), .out28(decoder_1_out0[28]),
    .out29(decoder_1_out0[29]), .out30(decoder_1_out0[30]), .out31(decoder_1_out0[31]), .sel(a3), .en(WE));
  s0_s7 s0_s7_1 (
    .in_1(decoder_1_out0[0]), .in_5(WD), .in_6(decoder_1_out0[1]), .in_7(decoder_1_out0[2]),
    .in_8(decoder_1_out0[3]), .in_9(decoder_1_out0[4]), .in_10(decoder_1_out0[5]), .in_11(decoder_1_out0[6]),
    .in_12(decoder_1_out0[7]), .out_13(s0_s7_1_out_13), .out_14(s0_s7_1_out_14), .out_15(s0_s7_1_out_15),
    .out_16(s0_s7_1_out_16), .out_17(s0_s7_1_out_17), .out_18(s0_s7_1_out_18), .out_19(s0_s7_1_out_19),
    .out_20(s0_s7_1_out_20), .in_2(in_2), .reset(reset), .WE(WE));
  _8_register u_8_register_1 (
    .in_1(decoder_1_out0[8]), .in_5(WD), .in_6(decoder_1_out0[9]), .in_7(decoder_1_out0[10]),
    .in_8(decoder_1_out0[11]), .in_9(decoder_1_out0[12]), .in_10(decoder_1_out0[13]),
    .in_11(decoder_1_out0[14]), .in_12(decoder_1_out0[15]), .out_13(n8_register_1_out_13),
    .out_14(n8_register_1_out_14), .out_15(n8_register_1_out_15), .out_16(n8_register_1_out_16),
    .out_17(n8_register_1_out_17), .out_18(n8_register_1_out_18), .out_19(n8_register_1_out_19),
    .out_20(n8_register_1_out_20), .in_2(in_2), .reset(reset), .WE(WE));
  _8_register u_8_register_2 (
    .in_1(decoder_1_out0[16]), .in_5(WD), .in_6(decoder_1_out0[17]), .in_7(decoder_1_out0[18]),
    .in_8(decoder_1_out0[19]), .in_9(decoder_1_out0[20]), .in_10(decoder_1_out0[21]),
    .in_11(decoder_1_out0[22]), .in_12(decoder_1_out0[23]), .out_13(n8_register_2_out_13),
    .out_14(n8_register_2_out_14), .out_15(n8_register_2_out_15), .out_16(n8_register_2_out_16),
    .out_17(n8_register_2_out_17), .out_18(n8_register_2_out_18), .out_19(n8_register_2_out_19),
    .out_20(n8_register_2_out_20), .in_2(in_2), .reset(reset), .WE(WE));
  _8_register u_8_register_3 (
    .in_1(decoder_1_out0[24]), .in_5(WD), .in_6(decoder_1_out0[25]), .in_7(decoder_1_out0[26]),
    .in_8(decoder_1_out0[27]), .in_9(decoder_1_out0[28]), .in_10(decoder_1_out0[29]),
    .in_11(decoder_1_out0[30]), .in_12(decoder_1_out0[31]), .out_13(n8_register_3_out_13),
    .out_14(n8_register_3_out_14), .out_15(n8_register_3_out_15), .out_16(n8_register_3_out_16),
    .out_17(n8_register_3_out_17), .out_18(n8_register_3_out_18), .out_19(n8_register_3_out_19),
    .out_20(n8_register_3_out_20), .in_2(in_2), .reset(reset), .WE(WE));
  Multiplexer #(.select(5), .width(32), .disabled(0), .enable("false")) multiplexer_1 (
    .in0(s0_s7_1_out_13), .in1(s0_s7_1_out_14), .in2(s0_s7_1_out_15), .in3(s0_s7_1_out_16),
    .in4(s0_s7_1_out_17), .in5(s0_s7_1_out_18), .in6(s0_s7_1_out_19), .in7(s0_s7_1_out_20),
    .in8(n8_register_1_out_13), .in9(n8_register_1_out_14), .in10(n8_register_1_out_15),
    .in11(n8_register_1_out_16), .in12(n8_register_1_out_17), .in13(n8_register_1_out_18),
    .in14(n8_register_1_out_19), .in15(n8_register_1_out_20), .in16(n8_register_2_out_13),
    .in17(n8_register_2_out_14), .in18(n8_register_2_out_15), .in19(n8_register_2_out_16),
    .in20(n8_register_2_out_17), .in21(n8_register_2_out_18), .in22(n8_register_2_out_19),
    .in23(n8_register_2_out_20), .in24(n8_register_3_out_13), .in25(n8_register_3_out_14),
    .in26(n8_register_3_out_15), .in27(n8_register_3_out_16), .in28(n8_register_3_out_17),
    .in29(n8_register_3_out_18), .in30(n8_register_3_out_19), .in31(n8_register_3_out_20), .out(out_8),
    .sel(a1));
  Multiplexer #(.select(5), .width(32), .disabled(0), .enable("false")) multiplexer_2 (
    .in0(s0_s7_1_out_13), .in1(s0_s7_1_out_14), .in2(s0_s7_1_out_15), .in3(s0_s7_1_out_16),
    .in4(s0_s7_1_out_17), .in5(s0_s7_1_out_18), .in6(s0_s7_1_out_19), .in7(s0_s7_1_out_20),
    .in8(n8_register_1_out_13), .in9(n8_register_1_out_14), .in10(n8_register_1_out_15),
    .in11(n8_register_1_out_16), .in12(n8_register_1_out_17), .in13(n8_register_1_out_18),
    .in14(n8_register_1_out_19), .in15(n8_register_1_out_20), .in16(n8_register_2_out_13),
    .in17(n8_register_2_out_14), .in18(n8_register_2_out_15), .in19(n8_register_2_out_16),
    .in20(n8_register_2_out_17), .in21(n8_register_2_out_18), .in22(n8_register_2_out_19),
    .in23(n8_register_2_out_20), .in24(n8_register_3_out_13), .in25(n8_register_3_out_14),
    .in26(n8_register_3_out_15), .in27(n8_register_3_out_16), .in28(n8_register_3_out_17),
    .in29(n8_register_3_out_18), .in30(n8_register_3_out_19), .in31(n8_register_3_out_20), .out(out_9),
    .sel(a2));

  // Other names for the same wires on the sheet: clk = in_2
endmodule

module _8_register (
  input  in_1,
  input  in_2,
  input  reset,
  input  WE,
  input  [31:0] in_5,
  input  in_6,
  input  in_7,
  input  in_8,
  input  in_9,
  input  in_10,
  input  in_11,
  input  in_12,
  output [31:0] out_13,
  output [31:0] out_14,
  output [31:0] out_15,
  output [31:0] out_16,
  output [31:0] out_17,
  output [31:0] out_18,
  output [31:0] out_19,
  output [31:0] out_20
);

  one_register one_register_1 (.in_1(in_5), .clk(in_2), .out_5(out_13), .enable(in_1), .reset(reset));
  one_register one_register_2 (.in_1(in_5), .clk(in_2), .out_5(out_17), .enable(in_9), .reset(reset));
  one_register one_register_3 (.in_1(in_5), .clk(in_2), .out_5(out_14), .enable(in_6), .reset(reset));
  one_register one_register_4 (.in_1(in_5), .clk(in_2), .out_5(out_18), .enable(in_10), .reset(reset));
  one_register one_register_5 (.in_1(in_5), .clk(in_2), .out_5(out_15), .enable(in_7), .reset(reset));
  one_register one_register_6 (.in_1(in_5), .clk(in_2), .out_5(out_19), .enable(in_11), .reset(reset));
  one_register one_register_7 (.in_1(in_5), .clk(in_2), .out_5(out_16), .enable(in_8), .reset(reset));
  one_register one_register_8 (.in_1(in_5), .clk(in_2), .out_5(out_20), .enable(in_12), .reset(reset));

  // Other names for the same wires on the sheet: clk = in_2
endmodule

module s0_s7 (
  input  in_1,
  input  in_2,
  input  reset,
  input  WE,
  input  [31:0] in_5,
  input  in_6,
  input  in_7,
  input  in_8,
  input  in_9,
  input  in_10,
  input  in_11,
  input  in_12,
  output [31:0] out_13,
  output [31:0] out_14,
  output [31:0] out_15,
  output [31:0] out_16,
  output [31:0] out_17,
  output [31:0] out_18,
  output [31:0] out_19,
  output [31:0] out_20
);

  Register #(.width(32)) register_1 (.D({32{1'b0}}), .en(in_1), .Q(out_13), .clk(in_2), .clr(reset));
  one_register one_register_1 (.in_1(in_5), .clk(in_2), .out_5(out_17), .enable(in_9), .reset(reset));
  one_register one_register_2 (.in_1(in_5), .clk(in_2), .out_5(out_14), .enable(in_6), .reset(reset));
  one_register one_register_3 (.in_1(in_5), .clk(in_2), .out_5(out_18), .enable(in_10), .reset(reset));
  one_register one_register_4 (.in_1(in_5), .clk(in_2), .out_5(out_15), .enable(in_7), .reset(reset));
  one_register one_register_5 (.in_1(in_5), .clk(in_2), .out_5(out_19), .enable(in_11), .reset(reset));
  one_register one_register_6 (.in_1(in_5), .clk(in_2), .out_5(out_16), .enable(in_8), .reset(reset));
  one_register one_register_7 (.in_1(in_5), .clk(in_2), .out_5(out_20), .enable(in_12), .reset(reset));

  // Other names for the same wires on the sheet: clk = in_2
endmodule

module one_register (
  input  [31:0] in_1,
  input  enable,
  input  clk,
  input  reset,
  output [31:0] out_5
);

  Register #(.width(32)) register_1 (.D(in_1), .en(enable), .Q(out_5), .clk(clk), .clr(reset));
endmodule

module Controller (
  input  [5:0] func,
  input  [5:0] opcode,
  output RegDst,
  output ALUSrc,
  output MemtoReg,
  output RegWrite,
  output MemWrite,
  output nPC_sel,
  output [2:0] ExtOp,
  output [2:0] out_10
);

  wire addu_out, beq_out, lui_out, lw_out, not_1_out, not_2_out, not_3_out, not_4_out, not_5_out, not_6_out,
       not_7_out, not_8_out, not_9_out, not_10_out, not_11_out, not_12_out, not_13_out, ori_out, subu_out,
       sw_out;

  not not_1 (not_1_out, opcode[4]);
  not not_2 (not_2_out, opcode[5]);
  not not_3 (not_3_out, opcode[2]);
  not not_4 (not_4_out, opcode[3]);
  not not_5 (not_5_out, opcode[1]);
  not not_6 (not_6_out, opcode[0]);
  not not_7 (not_7_out, func[1]);
  and addu (addu_out, not_2_out, not_1_out, not_4_out, not_7_out, not_3_out, not_5_out, not_6_out);
  and subu (subu_out, not_2_out, not_1_out, not_4_out, func[1], not_3_out, not_5_out, not_6_out);
  and ori (ori_out, opcode[0], not_5_out, opcode[2], opcode[3], not_1_out, not_2_out);
  and lw (lw_out, opcode[0], opcode[1], not_3_out, not_4_out, not_1_out, opcode[5]);
  and sw (sw_out, opcode[0], opcode[1], not_3_out, opcode[3], not_1_out, opcode[5]);
  and beq (beq_out, not_6_out, not_5_out, opcode[2], not_4_out, not_1_out, not_2_out);
  and lui (lui_out, opcode[0], opcode[1], opcode[2], opcode[3], not_2_out, not_1_out);
  or or_1 (RegDst, addu_out, subu_out);
  or u_ALUSrc (ALUSrc, ori_out, lw_out, lui_out, sw_out);
  buf or_2 (MemtoReg, lw_out);  // OR_Gate
  or or_3 (RegWrite, subu_out, addu_out, ori_out, lui_out, lw_out);
  buf or_4 (MemWrite, sw_out);  // OR_Gate
  or or_5 (out_10[1], beq_out, ori_out);
  not not_8 (not_8_out, beq_out);
  not not_9 (not_9_out, lui_out);
  not not_10 (not_10_out, subu_out);
  not not_11 (not_11_out, ori_out);
  not not_12 (not_12_out, lw_out);
  not not_13 (not_13_out, sw_out);
  buf or_6 (nPC_sel, beq_out);  // OR_Gate
  or or_7 (out_10[0], subu_out, beq_out);
  buf or_8 (ExtOp[1], lui_out);  // OR_Gate
  or or_9 (ExtOp[0], sw_out, lw_out);

  assign ExtOp[2] = 1'b0;
  assign out_10[2] = 1'b0;

  // Other names for the same wires on the sheet: ALUOp[1:0] = out_10[1:0]
endmodule
