// Logisim project p3_25instr.circ as structural Verilog: 10 circuits, main circuit main
module main (
  input  in_1,
  output [31:0] out_2,
  output out_3,
  output [4:0] out_4,
  output [31:0] out_5,
  output out_6,
  output [4:0] out_7,
  output [31:0] out_8
);

  wire ALU_mem_to_reg, B_reg, beq, bne, branch, clk, com_0, great_than_0, GRF2_imm, j, jal_write,
       \jalr_jr_专用 , less_than_0, multiplexer_1_out, not_1_out, not_2_out, or_1_out, or_2_out, pc_4_write,
       PCBrc_out, rd_rtop, sltu, zero;
  wire [1:0] B_crtl, extop, less_great_zero;
  wire [2:0] ALUOp;
  wire [4:0] multiplexer_2_out;
  wire [31:0] ext_out_3, GRF_rd2, \jalr_rs值 , less_than_0_data, linkALU, multiplexer_5_out,
       multiplexer_6_out, multiplexer_7_out, multiplexer_8_out, multiplexer_9_out, multiplexer_10_out,
       multiplexer_11_out, multiplexer_12_out, multiplexer_15_out, not_zero_data, pc_1, pc_4, ram_1_data,
       zero_data, \加载字节模块_1_out_3 , \加载字节模块_2_out_3 ;
  wire [31:7] multiplexer_14_out;

  Clock clock_1 (.out(clk));
  not not_1 (not_1_out, zero);
  Multiplexer #(.select(2), .enable("false")) multiplexer_1 (
    .in0(zero), .in1(or_2_out), .in2(or_1_out), .in3(not_1_out), .out(multiplexer_1_out),
    .sel(less_great_zero));
  and PCBrc (PCBrc_out, multiplexer_1_out, branch);
  or or_1 (or_1_out, great_than_0, zero);
  or or_2 (or_2_out, zero, less_than_0);
  ifu Ifu (
    .PCBrc(PCBrc_out), .j(j), .\jalr_jr专用 (\jalr_jr_专用 ), .reset(in_1), .clk(clk), .\jalr_rs值 (\jalr_rs值 ),
    .\j指令pc_4输出 (pc_1), .out_8(out_2));
  controler CTRL (
    .opcode(out_2[31:26]), .func(out_2[5:0]), .ALUOp(ALUOp), .regwrite(out_3), .extop(extop),
    .branch(branch), .rt_rdop(rd_rtop), .GRF2_imm(GRF2_imm), .memwrite(out_6),
    .ALU_mem_to_reg(ALU_mem_to_reg), .j(j), .jal(jal_write), .B_to_reg(B_reg), .jalwrite(pc_4_write),
    .\jalr_专用 (\jalr_jr_专用 ), .com_0(com_0), .less_great_zero(less_great_zero), .beq_reg_write_1(beq),
    .bne(bne), .sltu(sltu));
  Multiplexer #(.width(5), .enable("false")) multiplexer_2 (
    .in0(out_2[20:16]), .in1(out_2[15:11]), .out(multiplexer_2_out), .sel(rd_rtop));
  \pc乘4单元  \pc乘4单元_1  (.in_1(pc_1), .out_2(pc_4));
  Multiplexer #(.width(5), .enable("false")) multiplexer_3 (
    .in0(multiplexer_2_out), .in1({5{1'b1}}), .out(out_4), .sel(jal_write));
  ext ext (.extin(out_2[15:0]), .out_3(ext_out_3), .extOp(extop));
  Multiplexer #(.width(32), .enable("false")) multiplexer_4 (
    .in0(multiplexer_5_out), .in1(less_than_0_data), .out(out_5), .sel(sltu));
  Multiplexer #(.width(32), .enable("false")) multiplexer_5 (
    .in0(multiplexer_7_out), .in1(not_zero_data), .out(multiplexer_5_out), .sel(bne));
  grf GRF (
    .clk(clk), .\寄存器reset (in_1), .\寄存器写使能 (out_3), .rs(out_2[25:21]), .rt(out_2[20:16]), .rd(out_4),
    .wd(out_5), .rd1(\jalr_rs值 ), .rd2(GRF_rd2));
  Multiplexer #(.width(32), .enable("false")) multiplexer_6 (
    .in0(multiplexer_9_out), .in1(pc_4), .out(multiplexer_6_out), .sel(pc_4_write));
  Multiplexer #(.width(32), .enable("false")) multiplexer_7 (
    .in0(multiplexer_6_out), .in1(zero_data), .out(multiplexer_7_out), .sel(beq));
  Multiplexer #(.width(32), .enable("false")) multiplexer_8 (
    .in0(GRF_rd2), .in1(ext_out_3), .out(multiplexer_8_out), .sel(GRF2_imm));
  Multiplexer #(.width(32), .enable("false")) multiplexer_9 (
    .in0(linkALU), .in1(multiplexer_15_out), .out(multiplexer_9_out), .sel(ALU_mem_to_reg));
  Multiplexer #(.width(32), .enable("false")) multiplexer_10 (
    .in0(linkALU), .in1(zero_data), .out(multiplexer_10_out), .sel(beq));
  Multiplexer #(.width(32), .enable("false")) multiplexer_11 (
    .in0(multiplexer_10_out), .in1(not_zero_data), .out(multiplexer_11_out), .sel(bne));
  \加载字节模块  \u_加载字节模块_1  (.B_crtl(B_crtl), .mem_input(GRF_rd2), .out_3(\加载字节模块_1_out_3 ));
  alu ALU (
    .input1(\jalr_rs值 ), .input2(multiplexer_12_out), .ALUOp(ALUOp), .out_4(linkALU), .out_6(zero),
    .out_7(less_than_0), .out_5(great_than_0));
  Multiplexer #(.width(32), .enable("false")) multiplexer_12 (
    .in0(multiplexer_8_out), .in1({32{1'b0}}), .out(multiplexer_12_out), .sel(com_0));
  Multiplexer #(.width(32), .enable("false")) multiplexer_13 (
    .in0(GRF_rd2), .in1(\加载字节模块_1_out_3 ), .out(out_8), .sel(B_reg));
  Multiplexer #(.width(32), .enable("false")) multiplexer_14 (
    .in0(multiplexer_11_out), .in1(less_than_0_data), .out({multiplexer_14_out, out_7, B_crtl}), .sel(sltu));
  Multiplexer #(.width(32), .enable("false")) multiplexer_15 (
    .in0(ram_1_data), .in1(\加载字节模块_2_out_3 ), .out(multiplexer_15_out), .sel(B_reg));
  RAM #(.addrWidth(5), .dataWidth(32), .bus("separate")) ram_1 (
    .addr(out_7), .din(out_8), .data(ram_1_data), .str(out_6), .clk(clk), .clr(in_1));  // open: sel, ld
  not not_2 (not_2_out, zero);
  assign less_than_0_data = {{31{1'b0}}, less_than_0};  // Bit_Extender bit_extender_1
  assign zero_data = {{31{1'b0}}, zero};  // Bit_Extender bit_extender_2
  assign not_zero_data = {{31{1'b0}}, not_2_out};  // Bit_Extender bit_extender_3
  \加载字节模块  \u_加载字节模块_2  (.B_crtl(B_crtl), .mem_input(ram_1_data), .out_3(\加载字节模块_2_out_3 ));

  // Other names for the same wires on the sheet: func[5:0] = out_2[5:0]; imm[15:0] = out_2[15:0]; Instr[31:0] = out_2;
  //   shamt[4:0] = out_2[10:6]; rd[4:0] = out_2[15:11]; MemAddr[4:0] = out_7; MemData[31:0] = out_8; MemWrite = out_6;
  //   opcode[5:0] = out_2[31:26]; RegAddr[4:0] = out_4; RegData[31:0] = out_5; RegWrite = out_3; reset = in_1;
  //   rs[4:0] = out_2[25:21]; rt[4:0] = out_2[20:16]

  // Notes on the sheet:
  //   32
  //   32位imm
endmodule

module alu (
  input  [31:0] input1,
  input  [31:0] input2,
  input  [2:0] ALUOp,
  output [31:0] out_4,
  output out_5,
  output out_6,
  output out_7
);

  wire [31:0] adder_1_out, and_1_out, or_1_out, shifter_1_out, shifter_2_out, subtractor_1_out;

  Shifter #(.width(32)) shifter_1 (.in(input2), .\dist (input1[4:0]), .out(shifter_1_out));
  Shifter #(.width(32), .shift("lr")) shifter_2 (.in(input2), .\dist (input1[4:0]), .out(shifter_2_out));
  assign and_1_out = input2 & input1;  // AND_Gate and_1, 32 bits wide
  assign or_1_out = input2 | input1;  // OR_Gate or_1, 32 bits wide
  Adder #(.width(32)) adder_1 (.a(input2), .b(input1), .out(adder_1_out));  // open: cin, cout
  Subtractor #(.width(32)) subtractor_1 (.a(input1), .b(input2), .out(subtractor_1_out));  // open: bin, bout
  Multiplexer #(.select(3), .width(32), .enable("false")) multiplexer_1 (
    .in0(and_1_out), .in1(or_1_out), .in2(adder_1_out), .in3(subtractor_1_out), .in4(shifter_1_out),
    .in5(shifter_2_out), .out(out_4), .sel(ALUOp));  // open: in6, in7
  Comparator #(.width(32)) comparator_1 (.a(out_4), .b({32{1'b0}}), .gt(out_5), .eq(out_6), .lt(out_7));
endmodule

module grf (
  input  clk,
  input  \寄存器reset ,
  input  \寄存器写使能 ,
  input  [4:0] rs,
  input  [4:0] rt,
  input  [4:0] rd,
  input  [31:0] wd,
  output [31:0] rd1,
  output [31:0] rd2
);

  \寄存器  \u_寄存器_1  (
    .re(\寄存器reset ), .clk(clk), .we(\寄存器写使能 ), .in_4(wd), .a3(rd), .a1(rs), .a2(rt), .out_8(rd1), .out_9(rd2));

  // Notes on the sheet:
  //   a2
  //   a1
  //   a3
  //   wd
  //   clk
  //   reset
  //   we
endmodule

module \寄存器  (
  input  re,
  input  clk,
  input  we,
  input  [31:0] in_4,
  input  [4:0] a3,
  input  [4:0] a1,
  input  [4:0] a2,
  output [31:0] out_8,
  output [31:0] out_9
);

  wire a, b, c, d, demultiplexer_2_out0, demultiplexer_2_out1, demultiplexer_2_out2, demultiplexer_2_out3,
       demultiplexer_2_out4, demultiplexer_2_out5, demultiplexer_2_out6, demultiplexer_2_out7, e, f, g, h, i,
       j, k, l, m, n, o, p, q, r, s, t, u, v, w, x;
  wire [31:0] _1, _2, _3, _4, _5, _6, _7, _8, _9, _10, _11, _12, _13, _14, _15, _16, _17, _18, _19, _20, _21,
       _22, _23, _24, _25, _26, _27, _28, _29, _30, _31, _32, demultiplexer_1_out0, demultiplexer_1_out1,
       demultiplexer_1_out2, demultiplexer_1_out3, demultiplexer_1_out4, demultiplexer_1_out5,
       demultiplexer_1_out6, demultiplexer_1_out7, demultiplexer_1_out8, demultiplexer_1_out9,
       demultiplexer_1_out10, demultiplexer_1_out11, demultiplexer_1_out12, demultiplexer_1_out13,
       demultiplexer_1_out14, demultiplexer_1_out15, demultiplexer_1_out16, demultiplexer_1_out17,
       demultiplexer_1_out18, demultiplexer_1_out19, demultiplexer_1_out20, demultiplexer_1_out21,
       demultiplexer_1_out22, demultiplexer_1_out23, demultiplexer_1_out24, demultiplexer_1_out25,
       demultiplexer_1_out26, demultiplexer_1_out27, demultiplexer_1_out28, demultiplexer_1_out29,
       demultiplexer_1_out30, demultiplexer_1_out31;

  Register #(.width(32)) register_1 (.D({32{1'b0}}), .en(demultiplexer_2_out0), .Q(_1), .clk(clk), .clr(re));
  Register #(.width(32)) register_2 (.D(demultiplexer_1_out8), .en(a), .Q(_9), .clk(clk), .clr(re));
  Register #(.width(32)) register_3 (.D(demultiplexer_1_out16), .en(i), .Q(_17), .clk(clk), .clr(re));
  Register #(.width(32)) register_4 (.D(demultiplexer_1_out24), .en(q), .Q(_25), .clk(clk), .clr(re));
  Register #(.width(32)) register_5 (.D(demultiplexer_1_out1), .en(demultiplexer_2_out1), .Q(_2), .clk(clk), .clr(re));
  Register #(.width(32)) register_6 (.D(demultiplexer_1_out9), .en(b), .Q(_10), .clk(clk), .clr(re));
  Register #(.width(32)) register_7 (.D(demultiplexer_1_out17), .en(j), .Q(_18), .clk(clk), .clr(re));
  Register #(.width(32)) register_8 (.D(demultiplexer_1_out25), .en(r), .Q(_26), .clk(clk), .clr(re));
  Demultiplexer #(.select(5), .width(32), .tristate("true"), .enable("false")) demultiplexer_1 (
    .out0(demultiplexer_1_out0), .out1(demultiplexer_1_out1), .out2(demultiplexer_1_out2),
    .out3(demultiplexer_1_out3), .out4(demultiplexer_1_out4), .out5(demultiplexer_1_out5),
    .out6(demultiplexer_1_out6), .out7(demultiplexer_1_out7), .out8(demultiplexer_1_out8),
    .out9(demultiplexer_1_out9), .out10(demultiplexer_1_out10), .out11(demultiplexer_1_out11),
    .out12(demultiplexer_1_out12), .out13(demultiplexer_1_out13), .out14(demultiplexer_1_out14),
    .out15(demultiplexer_1_out15), .out16(demultiplexer_1_out16), .out17(demultiplexer_1_out17),
    .out18(demultiplexer_1_out18), .out19(demultiplexer_1_out19), .out20(demultiplexer_1_out20),
    .out21(demultiplexer_1_out21), .out22(demultiplexer_1_out22), .out23(demultiplexer_1_out23),
    .out24(demultiplexer_1_out24), .out25(demultiplexer_1_out25), .out26(demultiplexer_1_out26),
    .out27(demultiplexer_1_out27), .out28(demultiplexer_1_out28), .out29(demultiplexer_1_out29),
    .out30(demultiplexer_1_out30), .out31(demultiplexer_1_out31), .in(in_4), .sel(a3));
  Register #(.width(32)) register_9 (.D(demultiplexer_1_out2), .en(demultiplexer_2_out2), .Q(_3), .clk(clk), .clr(re));
  Register #(.width(32)) register_10 (.D(demultiplexer_1_out10), .en(c), .Q(_11), .clk(clk), .clr(re));
  Register #(.width(32)) register_11 (.D(demultiplexer_1_out18), .en(k), .Q(_19), .clk(clk), .clr(re));
  Register #(.width(32)) register_12 (.D(demultiplexer_1_out26), .en(s), .Q(_27), .clk(clk), .clr(re));
  Register #(.width(32)) register_13 (.D(demultiplexer_1_out3), .en(demultiplexer_2_out3), .Q(_4), .clk(clk), .clr(re));
  Register #(.width(32)) register_14 (.D(demultiplexer_1_out11), .en(d), .Q(_12), .clk(clk), .clr(re));
  Register #(.width(32)) register_15 (.D(demultiplexer_1_out19), .en(l), .Q(_20), .clk(clk), .clr(re));
  Register #(.width(32)) register_16 (.D(demultiplexer_1_out27), .en(t), .Q(_28), .clk(clk), .clr(re));
  Register #(.width(32)) register_17 (.D(demultiplexer_1_out4), .en(demultiplexer_2_out4), .Q(_5), .clk(clk), .clr(re));
  Register #(.width(32)) register_18 (.D(demultiplexer_1_out12), .en(e), .Q(_13), .clk(clk), .clr(re));
  Register #(.width(32)) register_19 (.D(demultiplexer_1_out20), .en(m), .Q(_21), .clk(clk), .clr(re));
  Register #(.width(32)) register_20 (.D(demultiplexer_1_out28), .en(u), .Q(_29), .clk(clk), .clr(re));
  Register #(.width(32)) register_21 (.D(demultiplexer_1_out5), .en(demultiplexer_2_out5), .Q(_6), .clk(clk), .clr(re));
  Register #(.width(32)) register_22 (.D(demultiplexer_1_out13), .en(f), .Q(_14), .clk(clk), .clr(re));
  Register #(.width(32)) register_23 (.D(demultiplexer_1_out21), .en(n), .Q(_22), .clk(clk), .clr(re));
  Register #(.width(32)) register_24 (.D(demultiplexer_1_out29), .en(v), .Q(_30), .clk(clk), .clr(re));
  Multiplexer #(.select(5), .width(32)) multiplexer_1 (
    .in0(_1), .in1(_2), .in2(_3), .in3(_4), .in4(_5), .in5(_6), .in6(_7), .in7(_8), .in8(_9), .in9(_10),
    .in10(_11), .in11(_12), .in12(_13), .in13(_14), .in14(_15), .in15(_16), .in16(_17), .in17(_18),
    .in18(_19), .in19(_20), .in20(_21), .in21(_22), .in22(_23), .in23(_24), .in24(_25), .in25(_26),
    .in26(_27), .in27(_28), .in28(_29), .in29(_30), .in30(_31), .in31(_32), .out(out_8), .sel(a1), .en(1'b1));
  Multiplexer #(.select(5), .width(32)) multiplexer_2 (
    .in0(_1), .in1(_2), .in2(_3), .in3(_4), .in4(_5), .in5(_6), .in6(_7), .in7(_8), .in8(_9), .in9(_10),
    .in10(_11), .in11(_12), .in12(_13), .in13(_14), .in14(_15), .in15(_16), .in16(_17), .in17(_18),
    .in18(_19), .in19(_20), .in20(_21), .in21(_22), .in22(_23), .in23(_24), .in24(_25), .in25(_26),
    .in26(_27), .in27(_28), .in28(_29), .in29(_30), .in30(_31), .in31(_32), .out(out_9), .sel(a2), .en(1'b1));
  Register #(.width(32)) register_25 (.D(demultiplexer_1_out6), .en(demultiplexer_2_out6), .Q(_7), .clk(clk), .clr(re));
  Register #(.width(32)) register_26 (.D(demultiplexer_1_out14), .en(g), .Q(_15), .clk(clk), .clr(re));
  Register #(.width(32)) register_27 (.D(demultiplexer_1_out22), .en(o), .Q(_23), .clk(clk), .clr(re));
  Register #(.width(32)) register_28 (.D(demultiplexer_1_out30), .en(w), .Q(_31), .clk(clk), .clr(re));
  Register #(.width(32)) register_29 (.D(demultiplexer_1_out7), .en(demultiplexer_2_out7), .Q(_8), .clk(clk), .clr(re));
  Register #(.width(32)) register_30 (.D(demultiplexer_1_out15), .en(h), .Q(_16), .clk(clk), .clr(re));
  Register #(.width(32)) register_31 (.D(demultiplexer_1_out23), .en(p), .Q(_24), .clk(clk), .clr(re));
  Register #(.width(32)) register_32 (.D(demultiplexer_1_out31), .en(x), .Q(_32), .clk(clk), .clr(re));
  Demultiplexer #(.select(5), .enable("false")) demultiplexer_2 (
    .out0(demultiplexer_2_out0), .out1(demultiplexer_2_out1), .out2(demultiplexer_2_out2),
    .out3(demultiplexer_2_out3), .out4(demultiplexer_2_out4), .out5(demultiplexer_2_out5),
    .out6(demultiplexer_2_out6), .out7(demultiplexer_2_out7), .out8(a), .out9(b), .out10(c), .out11(d),
    .out12(e), .out13(f), .out14(g), .out15(h), .out16(i), .out17(j), .out18(k), .out19(l), .out20(m),
    .out21(n), .out22(o), .out23(p), .out24(q), .out25(r), .out26(s), .out27(t), .out28(u), .out29(v),
    .out30(w), .out31(x), .in(we), .sel(a3));

  // Notes on the sheet:
  //   wd
  //   00000
  //   00001
  //   00010
  //   00011
  //   00100
  //   00101
  //   00111
  //   01000
endmodule

module ifu (
  input  PCBrc,
  input  j,
  input  \jalr_jr专用 ,
  input  reset,
  input  clk,
  input  [31:0] \jalr_rs值 ,
  output [31:0] \j指令pc_4输出 ,
  output [31:0] out_8
);

  wire _26, _27, _28, _29;
  wire [25:0] pc_pc;
  wire [31:0] adder_2_out, bit_extender_1_out, multiplexer_1_out, multiplexer_2_out, multiplexer_3_out;

  pc pc (.NPC(multiplexer_3_out[29:0]), .reset(reset), .clk(clk), .PC({_29, _28, _27, _26, pc_pc}));
  Adder #(.width(32)) adder_1 (
    .a({2'b00, _29, _28, _27, _26, pc_pc}), .b(32'h1), .out(\j指令pc_4输出 ), .cin(1'b0));  // open: cout
  ROM #(.addrWidth(5), .dataWidth(32)) rom_1 (.addr(pc_pc[4:0]), .data(out_8));  // open: sel
  assign bit_extender_1_out = {{16{out_8[15]}}, out_8[15:0]};  // Bit_Extender bit_extender_1
  Adder #(.width(32)) adder_2 (.a(\j指令pc_4输出 ), .b(bit_extender_1_out), .out(adder_2_out), .cin(1'b0));  // open: cout
  Multiplexer #(.width(32), .enable("false")) multiplexer_1 (
    .in0(\j指令pc_4输出 ), .in1(adder_2_out), .out(multiplexer_1_out), .sel(PCBrc));
  Multiplexer #(.width(32), .enable("false")) multiplexer_2 (
    .in0(multiplexer_1_out),
    .in1({2'b00, _29, _28, _27, _26, out_8[25:14], out_8[11:10], 2'b00, out_8[9:0]}),
    .out(multiplexer_2_out), .sel(j));
  Multiplexer #(.width(32), .enable("false")) multiplexer_3 (
    .in0(multiplexer_2_out), .in1({\jalr_rs值 [31:12], 2'b00, \jalr_rs值 [11:2]}), .out(multiplexer_3_out),
    .sel(\jalr_jr专用 ));

  // Notes on the sheet:
  //   PC+1
  //   IM 指令存储器
  //   contents of rom_1 (hex, n*v repeats v):
  //   34041234 3c051234 a43021 c53823 34080000 34090001 340a0001 340b0002 12b602b 12a682b 169702b 152a0002
  //   152b0003 ad070000 ad070004 152b0009 ad040008 ad05000c ad060010 ad070014 8d100008 8d11000c 8d120010
  //   8d130014 112afff4 ad100018 ad11001c
  //   PC+4
  //   pc+4+offset
  //   j指令专用sp
  //   pc除4器
endmodule

module pc (
  input  [29:0] NPC,
  input  reset,
  input  clk,
  output [29:0] PC
);

  wire comparator_1_eq;
  wire [29:0] adder_1_out, multiplexer_1_out, register_1_q;

  Register #(.width(30)) register_1 (.D(NPC), .en(1'b1), .Q(register_1_q), .clk(clk), .clr(reset));
  Comparator #(.width(30), .mode("unsigned")) comparator_1 (
    .a({30{1'b0}}), .b(register_1_q), .eq(comparator_1_eq));  // open: gt, lt
  Adder #(.width(30)) adder_1 (.a(register_1_q), .b(30'h3000), .out(adder_1_out), .cin(1'b0));  // open: cout
  Multiplexer #(.width(30), .enable("false")) multiplexer_1 (
    .in0(register_1_q), .in1(adder_1_out), .out(multiplexer_1_out), .sel(comparator_1_eq));
  Multiplexer #(.width(30), .enable("false")) multiplexer_2 (
    .in0(register_1_q), .in1(multiplexer_1_out), .out(PC), .sel(1'b1));
endmodule

module ext (
  input  [15:0] extin,
  input  [1:0] extOp,
  output [31:0] out_3
);

  wire [31:0] bit_extender_1_out, bit_extender_2_out;

  assign bit_extender_1_out = {{16{1'b0}}, extin};  // Bit_Extender bit_extender_1
  assign bit_extender_2_out = {{16{extin[15]}}, extin};  // Bit_Extender bit_extender_2
  Multiplexer #(.select(2), .width(32), .enable("false")) multiplexer_1 (
    .in0(bit_extender_1_out), .in1(bit_extender_2_out), .in2({extin, {16{1'b0}}}), .out(out_3), .sel(extOp));  // open: in3
endmodule

module controler (
  input  [5:0] opcode,
  input  [5:0] func,
  output regwrite,
  output [1:0] extop,
  output branch,
  output rt_rdop,
  output ALU_mem_to_reg,
  output GRF2_imm,
  output memwrite,
  output j,
  output jal,
  output B_to_reg,
  output jalwrite,
  output com_0,
  output \jalr_专用 ,
  output [1:0] less_great_zero,
  output beq_reg_write_1,
  output bne,
  output sltu,
  output [2:0] ALUOp
);

  wire addu_out, beq_out, bgez_out, Blez_out, bne_out, j_out, jal_out, jalr_out, jr_out, lbu_out, lui_out,
       lw_out, not_1_out, not_2_out, not_3_out, not_4_out, not_5_out, not_6_out, not_7_out, not_8_out,
       not_9_out, not_10_out, not_11_out, not_12_out, ori_out, sb_out, sllv_out, sltu_out, srlv_out,
       subu_out, sw_out;

  not not_1 (not_1_out, opcode[5]);
  not not_2 (not_2_out, opcode[4]);
  not not_3 (not_3_out, opcode[3]);
  not not_4 (not_4_out, opcode[2]);
  not not_5 (not_5_out, opcode[1]);
  not not_6 (not_6_out, opcode[0]);
  not not_7 (not_7_out, func[5]);
  not not_8 (not_8_out, func[3]);
  not not_9 (not_9_out, func[0]);
  not not_10 (not_10_out, func[4]);
  not not_11 (not_11_out, func[1]);
  not not_12 (not_12_out, func[2]);
  and addu (addu_out, not_1_out, not_2_out, not_3_out, not_4_out, not_5_out, not_6_out, func[5], not_10_out, not_8_out, not_12_out, not_11_out, func[0]);
  and subu (subu_out, not_1_out, not_2_out, not_3_out, not_4_out, not_5_out, not_6_out, func[5], not_10_out, not_8_out, not_12_out, func[1], func[0]);
  and ori (ori_out, not_1_out, not_2_out, opcode[3], opcode[2], not_5_out, opcode[0]);
  and lw (lw_out, opcode[5], not_2_out, not_3_out, not_4_out, opcode[1], opcode[0]);
  and sw (sw_out, opcode[5], not_2_out, opcode[3], not_4_out, opcode[1], opcode[0]);
  and beq (beq_out, not_1_out, not_2_out, not_3_out, opcode[2], not_5_out, not_6_out);
  and lui (lui_out, not_1_out, not_2_out, opcode[3], opcode[2], opcode[1], opcode[0]);
  and Blez (Blez_out, not_1_out, not_2_out, not_3_out, opcode[2], opcode[1], not_6_out);
  and u_jal (jal_out, not_1_out, not_2_out, not_3_out, not_4_out, opcode[1], opcode[0]);
  and u_j (j_out, not_1_out, not_2_out, not_3_out, not_4_out, opcode[1], not_6_out);
  and lbu (lbu_out, opcode[5], not_2_out, not_3_out, opcode[2], not_5_out, not_6_out);
  and sb (sb_out, opcode[5], not_2_out, opcode[3], not_4_out, not_5_out, not_6_out);
  and jalr (jalr_out, not_1_out, not_2_out, not_3_out, not_4_out, not_5_out, not_6_out, not_7_out, not_10_out, func[3], not_12_out, not_11_out, func[0]);
  and bgez (bgez_out, not_1_out, not_2_out, not_3_out, not_4_out, not_5_out, opcode[0]);
  and sllv (sllv_out, not_1_out, not_2_out, not_3_out, not_4_out, not_5_out, not_6_out, not_7_out, not_10_out, not_8_out, func[2], not_11_out, not_9_out);
  and srlv (srlv_out, not_1_out, not_2_out, not_3_out, not_4_out, not_5_out, not_6_out, not_7_out, not_10_out, not_8_out, func[2], func[1], not_9_out);
  and jr (jr_out, not_1_out, not_2_out, not_3_out, not_4_out, not_5_out, not_6_out, not_7_out, not_10_out, func[3], not_12_out, not_11_out, not_9_out);
  and u_bne (bne_out, not_1_out, not_2_out, not_3_out, opcode[2], not_5_out, opcode[0]);
  and u_sltu (sltu_out, not_1_out, not_2_out, not_3_out, not_4_out, not_5_out, not_6_out, func[5], not_10_out, func[3], not_12_out, func[1], func[0]);
  or ALUop1 (ALUOp[2], sllv_out, srlv_out);
  or ALUOp2 (ALUOp[1], sltu_out, bgez_out, addu_out, subu_out, Blez_out, lw_out, sw_out, beq_out, lui_out, jal_out, lbu_out, sb_out, bne_out);
  or ALUOp3 (ALUOp[0], ori_out, Blez_out, bgez_out, beq_out, srlv_out, bne_out, subu_out, sltu_out);
  or u_regwrite (regwrite, sltu_out, addu_out, subu_out, ori_out, lw_out, jal_out, lbu_out, lui_out, jalr_out, sllv_out, srlv_out);
  buf extop1 (extop[1], lui_out);  // OR_Gate
  buf extop2 (extop[0], 1'b0);  // OR_Gate
  or u_branch (branch, bne_out, bgez_out, Blez_out, beq_out);
  or u_rt_rdop (rt_rdop, srlv_out, sllv_out, addu_out, subu_out, Blez_out, jal_out, sltu_out, j_out, sb_out, jalr_out, bgez_out);
  or u_GRF2_imm (GRF2_imm, ori_out, lw_out, sw_out, lbu_out, lui_out, sb_out);
  or u_memwrite (memwrite, sw_out, sb_out);
  or u_ALU_mem_to_reg (ALU_mem_to_reg, lw_out, lbu_out);
  or j_2 (j, jal_out, j_out);
  buf jal_2 (jal, jal_out);  // OR_Gate
  or u_B_to_reg (B_to_reg, lbu_out, sb_out);
  or u_jalwrite (jalwrite, jal_out, jalr_out);
  or \u_jalr_专用  (\jalr_专用 , jr_out, jalr_out);
  buf u_com_0 (com_0, bgez_out);  // OR_Gate
  or less_great_zero_0 (less_great_zero[0], Blez_out, bne_out);
  or less_great_zero_1 (less_great_zero[1], bgez_out, bne_out);
  buf u_beq_reg_write_1 (beq_reg_write_1, beq_out);  // OR_Gate
  buf bne_2 (bne, bne_out);  // OR_Gate
  buf sltu_2 (sltu, sltu_out);  // OR_Gate
endmodule

module \加载字节模块  (
  input  [1:0] B_crtl,
  input  [31:0] mem_input,
  output [31:0] out_3
);

  wire [7:0] multiplexer_1_out;

  Multiplexer #(.select(2), .width(8), .enable("false")) multiplexer_1 (
    .in0(mem_input[7:0]), .in1(mem_input[15:8]), .in2(mem_input[23:16]), .in3(mem_input[31:24]),
    .out(multiplexer_1_out), .sel(B_crtl));
  assign out_3 = {{24{1'b0}}, multiplexer_1_out};  // Bit_Extender bit_extender_1
endmodule

module \pc乘4单元  (
  input  [31:0] in_1,
  output [31:0] out_2
);


  assign out_2 = {in_1[31:12], in_1[9:0], 2'b00};

  // Other names for the same wires on the sheet: _12 = in_1[12]
endmodule
